# Fritzing sketch circuit (saved by Fritzing 0.9.3b)
breadboards: 1

parts:
  Part1 = Arduino Uno (Rev3)
  R1 = Trimmer Potentiometer [maximum_resistance=10kΩ package=THT]
  LED1 = LED - 5mm [color="Red (633nm)" package="5 mm [THT]"]
  LED2 = LED - 5mm [color="Red (633nm)" package="5 mm [THT]"]
  S1 = Pushbutton [package="[THT]"]
  S2 = Pushbutton [package="[THT]"]
  R2 = Photocell (LDR) [package=THT]
  T1 = TMP36 Temperature Sensor [package="TO92 [THT]"]
  R3 = Resistor [tolerance=±5% resistance=220 package=THT]
  R7 = Resistor [tolerance=±5% resistance=10k package=THT]
  R10 = Resistor [tolerance=±5% resistance=220 package=THT]
  R11 = Resistor [tolerance=±5% resistance=10k package=THT]
  R12 = Resistor [tolerance=±5% resistance=10k package=THT]
  J1 = Basic Servo

nets:
  N1: Part1.A0, R1.wiper
  N2: Part1.A1, T1.Vout
  N3: Part1.A2, R2.pin_0, R7.Pin_1
  N4: Part1.D9_PWM, J1.pulse
  N5: Part1.D10_PWM/SS, S1.Pin_1, S1.Pin_2, R12.Pin_1
  N6: Part1.D11_PWM/MOSI, S2.Pin_1, S2.Pin_2, R11.Pin_1
  N7: Part1.D12/MISO, LED2.anode
  N8: Part1.D13/SCK, LED1.anode
  5V: Part1.5V, R1.leg2, R2.pin_1, T1.+Vs, R11.Pin_0, R12.Pin_0, J1.vcc
  GND: Part1.GND, T1.GND, R3.Pin_1, R10.Pin_1
  N9: R1.leg1, S1.Pin_3, S1.Pin_4, S2.Pin_3, S2.Pin_4, R7.Pin_0, J1.gnd
  N10: LED1.cathode, R3.Pin_0
  N11: LED2.cathode, R10.Pin_0
